// Logisim project Kiryushin_Smolin_Kenig_24215_tennis_ai + keyboard.circ as structural Verilog: 6 circuits, main circuit main
module main (
  input  rg,
  input  [2:0] vx,
  input  [7:0] x,
  input  [7:0] y,
  input  [2:0] vy,
  input  [4:0] bat_l,
  input  start,
  output [4:0] out_8
);

  wire and_3_out, and_4_out, and_5_out, and_6_out, and_7_out, and_8_out, cdm_8_mark5_1_p1, cdm_8_mark5_1_p2,
       cdm_8_mark5_1_p4, cdm_8_mark5_1_p5, cdm_8_mark5_1_p6, cdm_8_mark5_1_p7, cdm_8_mark5_1_p8,
       cdm_8_mark5_1_p9, cdm_8_mark5_1_p10, clear, clock, data, decoder_1_out1, decoder_1_out2,
       decoder_1_out3, decoder_1_out4, decoder_1_out5, decoder_1_out6, I_O_sel, ins, multiplexer_3_out,
       nand_1_out, not_1_out, not_2_out, not_3_out, or_1_out, RAM, rd_wr;
  wire [2:0] register_5_q;
  wire [3:0] I_O_adr;
  wire [7:0] bit_extender_1_out, cdm_8_mark5_1_p13, cdm_8_mark5_1_p14, I_O_data, multiplexer_1_out,
       multiplexer_2_out, multiplexer_4_out, register_1_q, register_2_q, register_3_q, register_4_q;
  wire [7:4] cdm_8_mark5_1_p12;

  Decoder #(.select(4), .disabled(0), .enable("false")) decoder_1 (
    .out1(decoder_1_out1), .out2(decoder_1_out2), .out3(decoder_1_out3), .out4(decoder_1_out4),
    .out5(decoder_1_out5), .out6(decoder_1_out6), .sel(I_O_adr));  // open: out0, out7, out8, out9, out10, out11, out12, out13, out14, out15
  // Probe on cdm_8_mark5_1_p1
  and and_1 (I_O_sel, ~nand_1_out, clock, data);  // AND_Gate
  Multiplexer #(.width(8), .disabled(0), .enable("false")) multiplexer_1 (
    .in0({8{1'b0}}), .in1(8'h1), .out(multiplexer_1_out), .sel(vx[2]));
  assign bit_extender_1_out = {{5{vy[2]}}, vy};  // Bit_Extender bit_extender_1
  Multiplexer #(.width(8), .disabled(0), .enable("false")) multiplexer_2 (
    .in0({8{1'b0}}), .in1(8'h1), .out(multiplexer_2_out), .sel(bat_l[4]));
  // Probe on cdm_8_mark5_1_p4
  // Probe on cdm_8_mark5_1_p2
  // Probe on cdm_8_mark5_1_p6
  Clock clock_1 (.out(clock));
  and and_2 (RAM, nand_1_out, data);
  Register register_1 (.D(x), .Q(register_1_q), .clk(multiplexer_3_out));  // open: en, clr
  Multiplexer #(.disabled(0), .enable("false")) multiplexer_3 (
    .in0(not_2_out), .in1(not_1_out), .out(multiplexer_3_out), .sel(start));
  not not_1 (not_1_out, start);
  not not_2 (not_2_out, vx[2]);
  // Probe on cdm_8_mark5_1_p5
  // Probe on cdm_8_mark5_1_p8
  // Probe on cdm_8_mark5_1_p7
  // CdM_8_mark5 cdm_8_mark5_1: pin names not known; wires that end beside it: cdm_8_mark5_1_p1, cdm_8_mark5_1_p2, clock, cdm_8_mark5_1_p4, cdm_8_mark5_1_p5, cdm_8_mark5_1_p6, cdm_8_mark5_1_p7, cdm_8_mark5_1_p8, cdm_8_mark5_1_p9, cdm_8_mark5_1_p10, rd_wr, {cdm_8_mark5_1_p12, I_O_adr}, cdm_8_mark5_1_p13, cdm_8_mark5_1_p14
  assign cdm_8_mark5_1_p14 = rd_wr ? I_O_data : 8'bz;  // Controlled_Buffer controlled_buffer_1
  nand nand_1 (nand_1_out, cdm_8_mark5_1_p12[4], cdm_8_mark5_1_p12[5], cdm_8_mark5_1_p12[6], cdm_8_mark5_1_p12[7]);
  and and_3 (and_3_out, rd_wr, I_O_sel, decoder_1_out1);
  and and_4 (and_4_out, rd_wr, decoder_1_out2, I_O_sel);
  and and_5 (and_5_out, rd_wr, decoder_1_out3, I_O_sel);
  and and_6 (and_6_out, rd_wr, decoder_1_out4, I_O_sel);
  and and_7 (and_7_out, ~rd_wr, I_O_sel, decoder_1_out5);  // AND_Gate
  and and_8 (and_8_out, rd_wr, I_O_sel, decoder_1_out6);
  Register register_2 (.D(y), .Q(register_2_q), .clk(multiplexer_3_out));  // open: en, clr
  Register register_3 (.D(bit_extender_1_out), .Q(register_3_q), .clk(multiplexer_3_out));  // open: en, clr
  Register register_4 (.D(multiplexer_2_out), .Q(register_4_q), .clk(multiplexer_3_out));  // open: en, clr
  Decoder #(.disabled(0)) decoder_2 (.out0(ins), .out1(data), .sel(cdm_8_mark5_1_p9), .en(cdm_8_mark5_1_p10));
  assign I_O_data = not_3_out ? cdm_8_mark5_1_p13 : 8'bz;  // Controlled_Buffer controlled_buffer_2
  not not_3 (not_3_out, rd_wr);
  assign I_O_data = and_3_out ? multiplexer_1_out : 8'bz;  // Controlled_Buffer controlled_buffer_3
  assign I_O_data = and_4_out ? register_1_q : 8'bz;  // Controlled_Buffer controlled_buffer_4
  assign I_O_data = and_5_out ? register_2_q : 8'bz;  // Controlled_Buffer controlled_buffer_5
  assign I_O_data = and_6_out ? register_3_q : 8'bz;  // Controlled_Buffer controlled_buffer_6
  assign I_O_data = and_8_out ? register_4_q : 8'bz;  // Controlled_Buffer controlled_buffer_7
  Multiplexer #(.width(8), .disabled(0), .enable("false")) multiplexer_4 (
    .in0(I_O_data), .in1(8'h70), .out(multiplexer_4_out), .sel(rg));
  or or_1 (or_1_out, and_7_out, rg);
  Register #(.trigger("falling")) register_5 (
    .D(multiplexer_4_out), .Q({out_8, register_5_q}), .clk(or_1_out));  // open: en, clr
  ROM rom_1 (.addr({cdm_8_mark5_1_p12, I_O_adr}), .data(I_O_data), .sel(ins));
  RAM #(.bus("separate")) ram_1 (
    .addr({cdm_8_mark5_1_p12, I_O_adr}), .din(I_O_data), .data(I_O_data), .sel(RAM), .clk(clock), .ld(rd_wr),
    .clr(clear));  // open: str
  // Probe on I_O_data
  // Probe on I_O_data

  // Other names for the same wires on the sheet: check = vx[2]

  // Notes on the sheet:
  //   contents of rom_1 (hex, n*v repeats v):
  //   d1 f1 b5 5 e0 d d0 f5 d1 70 a1 ee 0 d0 f2 b0 84 d1 e4 11 99 d0 7f 41 d0 f4 b0 d3 f3 bf 0 e1 23 ee 31
  //   0 e5 2e 85 17 e2 31 eb 4c ee 31 17 e2 4c d2 f6 ba a e1 40 d0 f0 e 12 e2 3f ee 40 13 d0 f0 e 38 e2 50
  //   d1 f5 a7 ee 0 d4 87 8b ee 31 d0 f8 13 ee 40
endmodule

module keyboard (
  input  [6:0] in_1,
  output [1:0] out_2
);

  wire comparator_1_eq, comparator_2_eq, comparator_3_eq, comparator_4_eq;

  Comparator #(.width(7)) comparator_1 (.a(in_1), .b(7'b1110011), .eq(comparator_1_eq));  // open: gt, lt
  Comparator #(.width(7)) comparator_2 (.a(in_1), .b(7'b1001011), .eq(comparator_2_eq));  // open: gt, lt
  Comparator #(.width(7)) comparator_3 (.a(in_1), .b(7'b1110111), .eq(comparator_3_eq));  // open: gt, lt
  Comparator #(.width(7)) comparator_4 (.a(in_1), .b(7'b1000110), .eq(comparator_4_eq));  // open: gt, lt
  Transistor #(.\type ("n")) transistor_1 (.in(1'b1), .out(out_2[0]), .gate(comparator_1_eq));
  Pull_Resistor pull_resistor_1 (.node(out_2[0]));
  Transistor #(.\type ("n"), .gate("br")) transistor_2 (.in(1'b1), .out(out_2[0]), .gate(comparator_2_eq));
  Transistor #(.\type ("n")) transistor_3 (.in(1'b1), .out(out_2[1]), .gate(comparator_3_eq));
  Pull_Resistor pull_resistor_2 (.node(out_2[1]));
  Transistor #(.\type ("n"), .gate("br")) transistor_4 (.in(1'b1), .out(out_2[1]), .gate(comparator_4_eq));
  // Probe on out_2
endmodule

module keyboardR (
  input  [6:0] in_1,
  output [1:0] out_2
);

  wire comparator_1_eq, comparator_2_eq, comparator_3_eq, comparator_4_eq;

  Comparator #(.width(7)) comparator_1 (.a(in_1), .b(7'b1101100), .eq(comparator_1_eq));  // open: gt, lt
  Comparator #(.width(7)) comparator_2 (.a(in_1), .b(7'b0110100), .eq(comparator_2_eq));  // open: gt, lt
  Comparator #(.width(7)) comparator_3 (.a(in_1), .b(7'b1101111), .eq(comparator_3_eq));  // open: gt, lt
  Comparator #(.width(7)) comparator_4 (.a(in_1), .b(7'b1001001), .eq(comparator_4_eq));  // open: gt, lt
  Transistor #(.\type ("n")) transistor_1 (.in(1'b1), .out(out_2[0]), .gate(comparator_1_eq));
  Pull_Resistor pull_resistor_1 (.node(out_2[0]));
  Transistor #(.\type ("n"), .gate("br")) transistor_2 (.in(1'b1), .out(out_2[0]), .gate(comparator_2_eq));
  Transistor #(.\type ("n")) transistor_3 (.in(1'b1), .out(out_2[1]), .gate(comparator_3_eq));
  Pull_Resistor pull_resistor_2 (.node(out_2[1]));
  Transistor #(.\type ("n"), .gate("br")) transistor_4 (.in(1'b1), .out(out_2[1]), .gate(comparator_4_eq));
  // Probe on out_2
endmodule

module test (
);

  wire clock_1_out;
  wire [6:0] keyboard_1_data;

  Clock clock_1 (.out(clock_1_out));
  Keyboard keyboard_1 (.clk(clock_1_out), .data(keyboard_1_data));  // open: re, clr, avail
  // Probe on keyboard_1_data
endmodule

module keyboardBML (
  input  [6:0] in_1,
  output [1:0] out_2
);

  wire comparator_1_eq, comparator_2_eq, comparator_3_eq, comparator_4_eq;

  Comparator #(.width(7)) comparator_1 (.a(in_1), .b(7'b1100101), .eq(comparator_1_eq));  // open: gt, lt
  Comparator #(.width(7)) comparator_2 (.a(in_1), .b(7'b1000011), .eq(comparator_2_eq));  // open: gt, lt
  Comparator #(.width(7)) comparator_3 (.a(in_1), .b(7'b0110010), .eq(comparator_3_eq));  // open: gt, lt
  Comparator #(.width(7)) comparator_4 (.a(in_1), .b(7'b1100100), .eq(comparator_4_eq));  // open: gt, lt
  Transistor #(.\type ("n")) transistor_1 (.in(1'b1), .out(out_2[0]), .gate(comparator_1_eq));
  Pull_Resistor pull_resistor_1 (.node(out_2[0]));
  Transistor #(.\type ("n"), .gate("br")) transistor_2 (.in(1'b1), .out(out_2[0]), .gate(comparator_2_eq));
  Transistor #(.\type ("n")) transistor_3 (.in(1'b1), .out(out_2[1]), .gate(comparator_3_eq));
  Pull_Resistor pull_resistor_2 (.node(out_2[1]));
  Transistor #(.\type ("n"), .gate("br")) transistor_4 (.in(1'b1), .out(out_2[1]), .gate(comparator_4_eq));
  // Probe on out_2
endmodule

module keyboardBMR (
  input  [6:0] in_1,
  output [1:0] out_2
);

  wire comparator_1_eq, comparator_2_eq, comparator_3_eq, comparator_4_eq;

  Comparator #(.width(7)) comparator_1 (.a(in_1), .b(7'b1110000), .eq(comparator_1_eq));  // open: gt, lt
  Comparator #(.width(7)) comparator_2 (.a(in_1), .b(7'b0110111), .eq(comparator_2_eq));  // open: gt, lt
  Comparator #(.width(7)) comparator_3 (.a(in_1), .b(7'b0110110), .eq(comparator_3_eq));  // open: gt, lt
  Comparator #(.width(7)) comparator_4 (.a(in_1), .b(7'b0111011), .eq(comparator_4_eq));  // open: gt, lt
  Transistor #(.\type ("n")) transistor_1 (.in(1'b1), .out(out_2[0]), .gate(comparator_1_eq));
  Pull_Resistor pull_resistor_1 (.node(out_2[0]));
  Transistor #(.\type ("n"), .gate("br")) transistor_2 (.in(1'b1), .out(out_2[0]), .gate(comparator_2_eq));
  Transistor #(.\type ("n")) transistor_3 (.in(1'b1), .out(out_2[1]), .gate(comparator_3_eq));
  Pull_Resistor pull_resistor_2 (.node(out_2[1]));
  Transistor #(.\type ("n"), .gate("br")) transistor_4 (.in(1'b1), .out(out_2[1]), .gate(comparator_4_eq));
  // Probe on out_2
endmodule
