// Logisim project Kiryushin_Smolin_Kenig_24215_tennis_tennis.circ as structural Verilog: 8 circuits, main circuit main
module main (
  input  goal_reset,
  input  AI,
  input  Stupidness
);

  wire button_1_out, clock;
  wire [1:0] controller_1_out_13, display_1_out_20, display_2_out_20, display_3_out_20;
  wire [4:0] controller_1_ballx, controller_1_bally, controller_1_out_10, controller_1_out_14,
       controller_1_out_15, display_1_out_15, display_1_out_16, display_1_out_17, display_1_out_18,
       display_1_out_19, display_2_out_15, display_2_out_16, display_2_out_17, display_2_out_18,
       display_2_out_19, display_3_out_15, display_3_out_16, display_3_out_17, display_3_out_18,
       display_3_out_19;
  wire [6:0] keyboard_1_data;
  wire [7:0] player1, player2;
  wire [31:0] display_1_out_7, display_1_out_8, display_1_out_9, display_1_out_10, display_1_out_11,
       display_1_out_12, display_1_out_13, display_1_out_14, display_2_out_7, display_2_out_8,
       display_2_out_9, display_2_out_10, display_2_out_11, display_2_out_12, display_2_out_13,
       display_2_out_14, display_3_out_7, display_3_out_8, display_3_out_9, display_3_out_10,
       display_3_out_11, display_3_out_12, display_3_out_13, display_3_out_14, display_4_out_7,
       display_4_out_8, display_4_out_9, display_4_out_10, display_4_out_11, display_4_out_12,
       display_4_out_13, display_4_out_14;

  Clock clock_1 (.out(clock));
  Keyboard keyboard_1 (.clk(clock), .data(keyboard_1_data));  // open: re, clr, avail
  Button button_1 (.out(button_1_out));
  Hex_Digit_Display hex_digit_display_1 (.value(player1[7:4]));  // open: dp
  Hex_Digit_Display hex_digit_display_2 (.value(player1[3:0]));  // open: dp
  DotMatrix #(.matrixcols(32), .matrixrows(32)) dotmatrix_1 (
    .col0(display_1_out_7), .col1(display_1_out_8), .col2(display_1_out_9), .col3(display_1_out_14),
    .col4(display_1_out_10), .col5(display_1_out_11), .col6(display_1_out_12), .col7(display_1_out_13),
    .col8(display_2_out_7), .col9(display_2_out_8), .col10(display_2_out_9), .col11(display_2_out_14),
    .col12(display_2_out_10), .col13(display_2_out_11), .col14(display_2_out_12), .col15(display_2_out_13),
    .col16(display_3_out_7), .col17(display_3_out_8), .col18(display_3_out_9), .col19(display_3_out_14),
    .col20(display_3_out_10), .col21(display_3_out_11), .col22(display_3_out_12), .col23(display_3_out_13),
    .col24(display_4_out_7), .col25(display_4_out_8), .col26(display_4_out_9), .col27(display_4_out_14),
    .col28(display_4_out_10), .col29(display_4_out_11), .col30(display_4_out_12), .col31(display_4_out_13));
  controller controller_1 (
    .keyboard_in(keyboard_1_data), .out_10(controller_1_out_10), .ballX(controller_1_ballx),
    .ballY(controller_1_bally), .out_14(controller_1_out_14), .out_7(player1), .out_8(player2),
    .in_1(button_1_out), .in_2(goal_reset), .in_3(clock), .in_4(AI), .in_5(Stupidness),
    .out_15(controller_1_out_15), .out_13(controller_1_out_13));  // open: out_12
  display display_1 (
    .in_1(controller_1_out_10), .in_2(controller_1_ballx), .in_3(controller_1_bally),
    .in_4(controller_1_out_14), .in_5(controller_1_out_15), .out_15(display_1_out_15),
    .out_16(display_1_out_16), .out_17(display_1_out_17), .out_18(display_1_out_18),
    .out_19(display_1_out_19), .out_9(display_1_out_9), .out_7(display_1_out_7), .out_8(display_1_out_8),
    .out_14(display_1_out_14), .out_10(display_1_out_10), .out_11(display_1_out_11),
    .out_12(display_1_out_12), .out_13(display_1_out_13), .in_6(controller_1_out_13),
    .out_20(display_1_out_20));
  display display_2 (
    .in_1(display_1_out_15), .in_2(display_1_out_16), .in_3(display_1_out_17), .in_4(display_1_out_18),
    .in_5(display_1_out_19), .out_15(display_2_out_15), .out_16(display_2_out_16), .out_17(display_2_out_17),
    .out_18(display_2_out_18), .out_19(display_2_out_19), .out_9(display_2_out_9), .out_7(display_2_out_7),
    .out_8(display_2_out_8), .out_14(display_2_out_14), .out_10(display_2_out_10), .out_11(display_2_out_11),
    .out_12(display_2_out_12), .out_13(display_2_out_13), .in_6(display_1_out_20), .out_20(display_2_out_20));
  display display_3 (
    .in_1(display_2_out_15), .in_2(display_2_out_16), .in_3(display_2_out_17), .in_4(display_2_out_18),
    .in_5(display_2_out_19), .out_15(display_3_out_15), .out_16(display_3_out_16), .out_17(display_3_out_17),
    .out_18(display_3_out_18), .out_19(display_3_out_19), .out_9(display_3_out_9), .out_7(display_3_out_7),
    .out_8(display_3_out_8), .out_14(display_3_out_14), .out_10(display_3_out_10), .out_11(display_3_out_11),
    .out_12(display_3_out_12), .out_13(display_3_out_13), .in_6(display_2_out_20), .out_20(display_3_out_20));
  display display_4 (
    .in_1(display_3_out_15), .in_2(display_3_out_16), .in_3(display_3_out_17), .in_4(display_3_out_18),
    .in_5(display_3_out_19), .out_9(display_4_out_9), .out_7(display_4_out_7), .out_8(display_4_out_8),
    .out_14(display_4_out_14), .out_10(display_4_out_10), .out_11(display_4_out_11),
    .out_12(display_4_out_12), .out_13(display_4_out_13), .in_6(display_3_out_20));  // open: out_15, out_16, out_17, out_18, out_19, out_20
  Hex_Digit_Display hex_digit_display_3 (.value(player2[7:4]));  // open: dp
  Hex_Digit_Display hex_digit_display_4 (.value(player2[3:0]));  // open: dp

  // Notes on the sheet:
  //   START
  //   0 - genious
  //   1 - stupid
endmodule

module inc (
  input  [4:0] in_1,
  output [4:0] out_2
);

  Adder #(.width(5)) adder_1 (.a(in_1), .b(5'b00001), .out(out_2));  // open: cin, cout
endmodule

module display (
  input  [4:0] in_1,
  input  [4:0] in_2,
  input  [4:0] in_3,
  input  [4:0] in_4,
  input  [4:0] in_5,
  input  [1:0] in_6,
  output [31:0] out_7,
  output [31:0] out_8,
  output [31:0] out_9,
  output [31:0] out_10,
  output [31:0] out_11,
  output [31:0] out_12,
  output [31:0] out_13,
  output [31:0] out_14,
  output [4:0] out_15,
  output [4:0] out_16,
  output [4:0] out_17,
  output [4:0] out_18,
  output [4:0] out_19,
  output [1:0] out_20
);

  wire _0, _1, _2, _3, _4, _5, _6, _7, comparator_1_eq, comparator_2_eq, comparator_3_eq;
  wire [4:0] divider_1_out, divider_1_rem;
  wire [31:0] l_bat32, multiplexer_2_out, multiplexer_4_out, multiplexer_13_out, multiplexer_16_out,
       multiplexer_26_out, multiplexer_36_out, multiplexer_38_out, multiplexer_40_out, or_1_out, or_2_out,
       or_3_out, or_4_out, or_5_out, or_6_out, or_7_out, or_8_out, pull_resistor_3_node,
       pull_resistor_5_node, r_bat32, state10, state11, state12, state13, state14, state15, state16, state17,
       state20, state21, state22, state23, state24, state25, state26, state27, state30, state31, state32,
       state33, state34, state35, state36, state37, y32;

  Multiplexer #(.select(2), .width(32), .disabled(0), .enable("false")) multiplexer_1 (
    .in0(or_1_out), .in1(state10), .in2(state20), .in3(state30), .out(out_7), .sel(in_6));
  assign or_1_out = {32{1'b0}} | multiplexer_2_out;  // OR_Gate or_1, 32 bits wide
  Multiplexer #(.width(32)) multiplexer_2 (.in0({32{1'b0}}), .in1(y32), .out(multiplexer_2_out), .sel(_0));  // open: en
  Pull_Resistor pull_resistor_1 (.node(_0));
  Multiplexer #(.select(2), .width(32), .disabled(0), .enable("false")) multiplexer_3 (
    .in0(or_2_out), .in1(state11), .in2(state21), .in3(state31), .out(out_8), .sel(in_6));
  assign or_2_out = {32{1'b0}} | multiplexer_4_out;  // OR_Gate or_2, 32 bits wide
  Multiplexer #(.width(32)) multiplexer_4 (.in0({32{1'b0}}), .in1(y32), .out(multiplexer_4_out), .sel(_1));  // open: en
  Pull_Resistor pull_resistor_2 (.node(_1));
  Comparator #(.width(5), .mode("unsigned")) comparator_1 (
    .a(in_1), .b({5{1'b0}}), .eq(comparator_1_eq));  // open: gt, lt
  Pull_Resistor pull_resistor_3 (.node(pull_resistor_3_node));
  assign pull_resistor_3_node = comparator_1_eq ? l_bat32 : 32'bz;  // Controlled_Buffer controlled_buffer_1
  Multiplexer #(.select(2), .width(32), .disabled(0), .enable("false")) multiplexer_5 (
    .in0(32'h8000), .in1(32'h9200), .in2({32{1'b0}}), .in3(32'h1004fe00), .out(state11), .sel(in_1[1:0]));
  Multiplexer #(.select(2), .width(32), .disabled(0), .enable("false")) multiplexer_6 (
    .in0(32'h8000), .in1({32{1'b0}}), .in2(32'hfe00), .in3(32'h10040000), .out(state12), .sel(in_1[1:0]));
  Multiplexer #(.select(2), .width(32), .disabled(0), .enable("false")) multiplexer_7 (
    .in0(32'hfe00), .in1(32'h7c0fe00), .in2(32'h1ffc8000), .in3(32'h10746200), .out(state13), .sel(in_1[1:0]));
  Multiplexer #(.select(2), .width(32), .disabled(0), .enable("false")) multiplexer_8 (
    .in0(32'h4008000), .in1(32'h208000), .in2(32'h10046000), .in3(32'h10049200), .out(state14),
    .sel(in_1[1:0]));
  Multiplexer #(.select(2), .width(32), .disabled(0), .enable("false")) multiplexer_9 (
    .in0(32'h4008000), .in1(32'h106000), .in2(32'h17041c00), .in3(32'h1ffc9200), .out(state15),
    .sel(in_1[1:0]));
  Multiplexer #(.select(2), .width(32), .disabled(0), .enable("false")) multiplexer_10 (
    .in0(32'h7f00000), .in1(32'h201c00), .in2(32'h10040200), .in3(32'h8c00), .out(state16), .sel(in_1[1:0]));
  Multiplexer #(.select(2), .width(32), .disabled(0), .enable("false")) multiplexer_11 (
    .in0(32'h400fe00), .in1(32'h7c00200), .in2(32'h1004fe00), .in3({32{1'b0}}), .out(state17), .sel(in_1[1:0]));
  Multiplexer #(.select(2), .width(32), .disabled(0), .enable("false")) multiplexer_12 (
    .in0(or_3_out), .in1(state12), .in2(state22), .in3(state32), .out(out_9), .sel(in_6));
  assign or_3_out = {32{1'b0}} | multiplexer_13_out;  // OR_Gate or_3, 32 bits wide
  Multiplexer #(.width(32)) multiplexer_13 (
    .in0({32{1'b0}}), .in1(y32), .out(multiplexer_13_out), .sel(_2));  // open: en
  Pull_Resistor pull_resistor_4 (.node(_2));
  Multiplexer #(.select(2), .width(32), .disabled(0), .enable("false")) multiplexer_14 (
    .in0({32{1'b0}}), .in1(32'h4009200), .in2(32'hfe00), .in3(32'h10840000), .out(state10), .sel(in_1[1:0]));
  Comparator #(.width(5), .mode("unsigned")) comparator_2 (
    .a(in_1), .b(5'b00011), .eq(comparator_2_eq));  // open: gt, lt
  inc inc_1 (.in_1(in_1), .out_2(out_15));
  Pull_Resistor pull_resistor_5 (.node(pull_resistor_5_node));
  assign pull_resistor_5_node = comparator_2_eq ? r_bat32 : 32'bz;  // Controlled_Buffer controlled_buffer_2
  Multiplexer #(.select(2), .width(32), .disabled(0), .enable("false")) multiplexer_15 (
    .in0(or_4_out), .in1(state13), .in2(state23), .in3(state33), .out(out_14), .sel(in_6));
  assign or_4_out = {32{1'b0}} | pull_resistor_3_node | multiplexer_16_out;  // OR_Gate or_4, 32 bits wide
  Multiplexer #(.width(32)) multiplexer_16 (
    .in0({32{1'b0}}), .in1(y32), .out(multiplexer_16_out), .sel(_3));  // open: en
  Pull_Resistor pull_resistor_6 (.node(_3));
  Multiplexer #(.select(2), .width(32), .disabled(0), .enable("false")) multiplexer_17 (
    .in0({32{1'b0}}), .in1(32'h1ff0), .in2(32'h1008), .in3(32'h1800), .out(state20), .sel(in_1[1:0]));
  Multiplexer #(.select(2), .width(32), .disabled(0), .enable("false")) multiplexer_18 (
    .in0({32{1'b0}}), .in1(32'h8), .in2(32'h1008), .in3(32'h600), .out(state21), .sel(in_1[1:0]));
  Multiplexer #(.select(2), .width(32), .disabled(0), .enable("false")) multiplexer_19 (
    .in0({32{1'b0}}), .in1(32'h8), .in2(32'h1ff8), .in3(32'h180), .out(state22), .sel(in_1[1:0]));
  Multiplexer #(.select(2), .width(32), .disabled(0), .enable("false")) multiplexer_20 (
    .in0(32'h1ffc1ff0), .in1(32'h8), .in2(32'h1008), .in3(32'h60), .out(state23), .sel(in_1[1:0]));
  Multiplexer #(.select(2), .width(32), .disabled(0), .enable("false")) multiplexer_21 (
    .in0(32'h11000008), .in1(32'h8), .in2(32'h1008), .in3(32'h18), .out(state24), .sel(in_1[1:0]));
  Multiplexer #(.select(2), .width(32), .disabled(0), .enable("false")) multiplexer_22 (
    .in0(32'h11000008), .in1(32'h1ffc1ff0), .in2({32{1'b0}}), .in3(32'h1ff8), .out(state25), .sel(in_1[1:0]));
  Multiplexer #(.select(2), .width(32), .disabled(0), .enable("false")) multiplexer_23 (
    .in0(32'h11000008), .in1({32{1'b0}}), .in2({32{1'b0}}), .in3({32{1'b0}}), .out(state26), .sel(in_1[1:0]));
  Multiplexer #(.select(2), .width(32), .disabled(0), .enable("false")) multiplexer_24 (
    .in0(32'h1f000008), .in1({32{1'b0}}), .in2(32'h1ff8), .in3({32{1'b0}}), .out(state27), .sel(in_1[1:0]));
  Comparator #(.width(5)) comparator_3 (.a(in_1), .b(divider_1_out), .eq(comparator_3_eq));  // open: gt, lt
  Divider #(.width(5)) divider_1 (.a(in_2), .b(5'b01000), .out(divider_1_out), .rem(divider_1_rem));  // open: upper
  Multiplexer #(.select(2), .width(32), .disabled(0), .enable("false")) multiplexer_25 (
    .in0(or_5_out), .in1(state14), .in2(state24), .in3(state34), .out(out_10), .sel(in_6));
  assign or_5_out = {32{1'b0}} | pull_resistor_5_node | multiplexer_26_out;  // OR_Gate or_5, 32 bits wide
  Multiplexer #(.width(32)) multiplexer_26 (
    .in0({32{1'b0}}), .in1(y32), .out(multiplexer_26_out), .sel(_4));  // open: en
  Pull_Resistor pull_resistor_7 (.node(_4));
  Decoder #(.select(3)) decoder_1 (
    .out0(_0), .out1(_1), .out2(_2), .out3(_3), .out4(_4), .out5(_5), .out6(_6), .out7(_7),
    .sel(divider_1_rem[2:0]), .en(comparator_3_eq));
  Multiplexer #(.select(2), .width(32), .disabled(0), .enable("false")) multiplexer_27 (
    .in0({32{1'b0}}), .in1(32'h1ff0), .in2(32'he041008), .in3(32'h1800), .out(state30), .sel(in_1[1:0]));
  Multiplexer #(.select(2), .width(32), .disabled(0), .enable("false")) multiplexer_28 (
    .in0({32{1'b0}}), .in1(32'h8), .in2(32'h1008), .in3(32'h600), .out(state31), .sel(in_1[1:0]));
  Multiplexer #(.select(2), .width(32), .disabled(0), .enable("false")) multiplexer_29 (
    .in0({32{1'b0}}), .in1(32'h8), .in2(32'h1ff8), .in3(32'h180), .out(state32), .sel(in_1[1:0]));
  Multiplexer #(.select(2), .width(32), .disabled(0), .enable("false")) multiplexer_30 (
    .in0(32'h1ffc1ff0), .in1(32'h103c0008), .in2(32'h1008), .in3(32'h60), .out(state33), .sel(in_1[1:0]));
  Multiplexer #(.select(2), .width(32), .disabled(0), .enable("false")) multiplexer_31 (
    .in0(32'h11000008), .in1(32'h10440008), .in2(32'h1008), .in3(32'h18), .out(state34), .sel(in_1[1:0]));
  Multiplexer #(.select(2), .width(32), .disabled(0), .enable("false")) multiplexer_32 (
    .in0(32'h11000008), .in1(32'h10841ff0), .in2({32{1'b0}}), .in3(32'h1ff8), .out(state35), .sel(in_1[1:0]));
  Multiplexer #(.select(2), .width(32), .disabled(0), .enable("false")) multiplexer_33 (
    .in0(32'h11000008), .in1(32'h10840000), .in2({32{1'b0}}), .in3({32{1'b0}}), .out(state36), .sel(in_1[1:0]));
  Multiplexer #(.select(2), .width(32), .disabled(0), .enable("false")) multiplexer_34 (
    .in0(32'h1f000008), .in1(32'h11040000), .in2(32'h1ff8), .in3({32{1'b0}}), .out(state37), .sel(in_1[1:0]));
  Pull_Resistor pull_resistor_8 (.node(_5));
  Multiplexer #(.select(2), .width(32), .disabled(0), .enable("false")) multiplexer_35 (
    .in0(or_6_out), .in1(state15), .in2(state25), .in3(state35), .out(out_11), .sel(in_6));
  assign or_6_out = {32{1'b0}} | multiplexer_36_out;  // OR_Gate or_6, 32 bits wide
  Multiplexer #(.width(32)) multiplexer_36 (
    .in0({32{1'b0}}), .in1(y32), .out(multiplexer_36_out), .sel(_5));  // open: en
  assign or_7_out = {32{1'b0}} | multiplexer_38_out;  // OR_Gate or_7, 32 bits wide
  Pull_Resistor pull_resistor_9 (.node(_6));
  Multiplexer #(.select(2), .width(32), .disabled(0), .enable("false")) multiplexer_37 (
    .in0(or_7_out), .in1(state16), .in2(state26), .in3(state36), .out(out_12), .sel(in_6));
  Multiplexer #(.width(32)) multiplexer_38 (
    .in0({32{1'b0}}), .in1(y32), .out(multiplexer_38_out), .sel(_6));  // open: en
  Shifter #(.width(32)) shifter_1 (.in(32'h1), .\dist (in_3), .out(y32));
  Shifter #(.width(32)) shifter_2 (.in(32'h7), .\dist (in_4), .out(l_bat32));
  Shifter #(.width(32)) shifter_3 (.in(32'h7), .\dist (in_5), .out(r_bat32));
  Multiplexer #(.select(2), .width(32), .disabled(0), .enable("false")) multiplexer_39 (
    .in0(or_8_out), .in1(state17), .in2(state27), .in3(state37), .out(out_13), .sel(in_6));
  assign or_8_out = {32{1'b0}} | multiplexer_40_out;  // OR_Gate or_8, 32 bits wide
  Multiplexer #(.width(32)) multiplexer_40 (
    .in0({32{1'b0}}), .in1(y32), .out(multiplexer_40_out), .sel(_7));  // open: en
  Pull_Resistor pull_resistor_10 (.node(_7));

  assign out_16 = in_2;
  assign out_17 = in_3;
  assign out_18 = in_4;
  assign out_19 = in_5;
  assign out_20 = in_6;

  // Other names for the same wires on the sheet: id[1:0] = in_1[1:0]; l_bat[4:0] = in_4; r_bat[4:0] = in_5;
  //   state[1:0] = in_6; y[4:0] = in_3
endmodule

module controller (
  input  in_1,
  input  in_2,
  input  in_3,
  input  in_4,
  input  in_5,
  input  [6:0] keyboard_in,
  output [7:0] out_7,
  output [7:0] out_8,
  output [4:0] ballX,
  output [4:0] out_10,
  output [4:0] ballY,
  output [3:0] out_12,
  output [1:0] out_13,
  output [4:0] out_14,
  output [4:0] out_15
);

  wire _1, _2, adder_1_cout, adder_2_cout, and_2_out, and_3_out, and_4_out, and_5_out, and_6_out, and_7_out,
       and_8_out, and_9_out, and_10_out, and_11_out, and_12_out, and_13_out, and_14_out, and_15_out,
       and_16_out, and_17_out, bot, center, cg2, ch, ch2, check_collision_2_out_8, check_collision_3_out_8,
       clock, col, comparator_1_eq, comparator_2_eq, comparator_3_gt, comparator_3_lt, comparator_4_gt,
       comparator_4_lt, comparator_5_eq, comparator_6_eq, comparator_7_eq, comparator_8_eq, comparator_9_gt,
       comparator_10_eq, comparator_10_gt, comparator_10_lt, controlled_buffer_1_out, counter_1_q,
       counter_3_carry, counter_4_carry, counter_5_carry, counter_7_carry, counter_8_carry, counter_9_carry,
       counter_10_carry, counter_11_carry, counter_14_carry, counter_16_carry, counter_17_q, d_ff_1_q,
       d_ff_2_q, d_ff_3_q, g, multiplexer_9_out, multiplexer_10_out, multiplexer_19_out, multiplexer_20_out,
       multiplexer_21_out, multiplexer_22_out, multiplexer_23_out, multiplexer_24_out, multiplexer_26_out,
       multiplexer_27_out, multiplexer_28_out, multiplexer_29_out, multiplexer_30_out, multiplexer_31_out,
       not_1_out, not_2_out, not_3_out, not_4_out, not_5_out, not_6_out, not_7_out, not_8_out, not_9_out,
       not_10_out, not_11_out, not_12_out, not_13_out, not_14_out, or_3_out, or_4_out, or_5_out, or_6_out,
       or_7_out, or_8_out, or_9_out, or_10_out, or_13_out, p1g, p2g, random_1_out, switch_x, switch_y, top,
       xor_1_out, xor_2_out;
  wire [1:0] keyboard_1_out_2, keyboardr_1_out_2, multiplexer_33_out, multiplexer_34_out, random_2_out,
       random_3_out, random_4_out, random_8_out, state;
  wire [2:0] aix, aiy, multiplexer_1_out, multiplexer_2_out, multiplexer_3_out, multiplexer_5_out,
       multiplexer_7_out, multiplexer_8_out, multiplexer_11_out, multiplexer_12_out, multiplexer_13_out,
       negator_1_out, negator_2_out, new_vx, new_vy, vx, vy;
  wire [3:0] random_7_out;
  wire [4:0] adder_1_out, adder_2_out, adder_3_out, bit_extender_1_out, main_1_out_8, multiplexer_14_out,
       multiplexer_16_out, multiplexer_17_out, multiplexer_18_out, multiplexer_25_out, random_5_out,
       subtractor_1_out, subtractor_2_out, subtractor_3_out;
  wire [5:0] random_6_out;
  wire [7:0] adder_4_out, adder_5_out, bit_extender_2_out, bit_extender_3_out, multiplexer_4_out,
       multiplexer_6_out, oldx, oldy, x, y;

  and and_1 (cg2, _1, in_2);
  or or_1 (ch, g, in_1);
  or or_2 (g, cg2, and_2_out);
  and and_2 (and_2_out, in_2, _2);
  Multiplexer #(.width(3), .enable("false")) multiplexer_1 (
    .in0(3'b110), .in1(3'b010), .out(multiplexer_1_out), .sel(cg2));
  Multiplexer #(.width(3), .enable("false")) multiplexer_2 (
    .in0(3'b010), .in1(3'b110), .out(multiplexer_2_out), .sel(random_1_out));
  Random #(.width(1)) random_1 (.clk(in_3), .out(random_1_out));  // open: next, clr
  Multiplexer #(.width(3), .enable("false")) multiplexer_3 (
    .in0(multiplexer_1_out), .in1(multiplexer_2_out), .out(multiplexer_3_out), .sel(in_1));
  Multiplexer #(.width(8), .enable("false")) multiplexer_4 (
    .in0({ballX, multiplexer_11_out}), .in1(8'h7f), .out(multiplexer_4_out), .sel(ch));
  Multiplexer #(.width(3), .enable("false")) multiplexer_5 (
    .in0(new_vx), .in1(multiplexer_3_out), .out(multiplexer_5_out), .sel(ch));
  Multiplexer #(.width(8), .enable("false")) multiplexer_6 (
    .in0({ballY, multiplexer_12_out}), .in1(8'h7f), .out(multiplexer_6_out), .sel(ch));
  Multiplexer #(.width(3), .enable("false")) multiplexer_7 (
    .in0(new_vy), .in1(3'b000), .out(multiplexer_7_out), .sel(ch));
  Adder #(.width(5)) adder_1 (.a(out_14), .b(5'b00011), .out(adder_1_out), .cout(adder_1_cout));  // open: cin
  Subtractor #(.width(5)) subtractor_1 (
    .a(out_14), .b(5'b00001), .out(subtractor_1_out), .bin(adder_1_cout));  // open: bout
  Comparator #(.width(5)) comparator_1 (.a(5'b00011), .b(ballX), .eq(comparator_1_eq));  // open: gt, lt
  keyboard keyboard_1 (.in_1(keyboard_in), .out_2(keyboard_1_out_2));
  keyboardR keyboardr_1 (.in_1(keyboard_in), .out_2(keyboardr_1_out_2));
  Adder #(.width(5)) adder_2 (.a(out_15), .b(5'b00011), .out(adder_2_out), .cout(adder_2_cout));  // open: cin
  Subtractor #(.width(5)) subtractor_2 (
    .a(out_15), .b(5'b00001), .out(subtractor_2_out), .bin(adder_2_cout));  // open: bout
  Comparator #(.width(5)) comparator_2 (.a(5'b11100), .b(ballX), .eq(comparator_2_eq));  // open: gt, lt
  Register u_x (.D(multiplexer_4_out), .Q(oldx), .clk(clock));  // open: en, clr
  Register #(.width(3)) u_vx (.D(multiplexer_5_out), .Q(aix), .clk(clock));  // open: en, clr
  Register u_y (.D(multiplexer_6_out), .Q(oldy), .clk(clock));  // open: en, clr
  motion motion_1 (.coord(oldy), .speed(aiy), .new_cords(y), .new_speed(vy));  // open: p1goal, p2goal
  Register #(.width(3)) u_vy (.D(multiplexer_7_out), .Q(aiy), .clk(clock));  // open: en, clr
  Comparator #(.width(2)) comparator_3 (
    .a(keyboard_1_out_2), .b(2'b00), .gt(comparator_3_gt), .lt(comparator_3_lt));  // open: eq
  Comparator #(.width(2)) comparator_4 (
    .a(keyboardr_1_out_2), .b(2'b00), .gt(comparator_4_gt), .lt(comparator_4_lt));  // open: eq
  Comparator #(.width(5)) comparator_5 (.a(adder_1_out), .b(ballY), .eq(comparator_5_eq));  // open: gt, lt
  Comparator #(.width(5)) comparator_6 (.a(subtractor_1_out), .b(ballY), .eq(comparator_6_eq));  // open: gt, lt
  not not_1 (not_1_out, comparator_3_lt);
  not not_2 (not_2_out, comparator_3_gt);
  not not_3 (not_3_out, comparator_3_lt);
  not not_4 (not_4_out, comparator_4_lt);
  not not_5 (not_5_out, comparator_4_gt);
  not not_6 (not_6_out, comparator_4_lt);
  Comparator #(.width(5)) comparator_7 (.a(adder_2_out), .b(ballY), .eq(comparator_7_eq));  // open: gt, lt
  Comparator #(.width(5)) comparator_8 (.a(subtractor_2_out), .b(ballY), .eq(comparator_8_eq));  // open: gt, lt
  motion motion_2 (.coord(oldx), .speed(aix), .p1goal(p1g), .p2goal(p2g), .new_cords(x), .new_speed(vx));
  or or_3 (or_3_out, comparator_5_eq, comparator_6_eq);
  and and_3 (and_3_out, or_3_out, comparator_1_eq);
  and and_4 (and_4_out, comparator_3_gt, not_1_out);
  and and_5 (and_5_out, not_2_out, comparator_3_lt);
  or or_4 (or_4_out, and_5_out, and_6_out);
  and and_6 (and_6_out, comparator_3_gt, not_3_out);
  and and_7 (and_7_out, comparator_4_gt, not_4_out);
  and and_8 (and_8_out, not_5_out, comparator_4_lt);
  or or_5 (or_5_out, and_8_out, and_9_out);
  and and_9 (and_9_out, comparator_4_gt, not_6_out);
  or or_6 (or_6_out, comparator_7_eq, comparator_8_eq);
  and and_10 (and_10_out, or_6_out, comparator_2_eq);
  and and_11 (and_11_out, ~and_3_out, or_4_out);  // AND_Gate
  and and_12 (and_12_out, or_5_out, ~and_10_out);  // AND_Gate
  or or_7 (or_7_out, switch_y, switch_x);
  Multiplexer #(.width(3), .enable("false")) multiplexer_8 (
    .in0(3'b010), .in1(3'b110), .out(multiplexer_8_out), .sel(xor_1_out));
  xor xor_1 (xor_1_out, vx[2], switch_x);
  Multiplexer #(.disabled(0), .enable("false")) multiplexer_9 (
    .in0(and_4_out), .in1(1'b1), .out(multiplexer_9_out), .sel(ch));
  Multiplexer #(.disabled(0), .enable("false")) multiplexer_10 (
    .in0(and_11_out), .in1(1'b0), .out(multiplexer_10_out), .sel(ch));
  Kiryushin_Smolin_Kenig_24215_tennis_ai___keyboard_main main_1 (
    .vx(aix), .x(oldx), .y(oldy), .vy(aiy), .bat_l(out_14), .start(ch), .out_8(main_1_out_8), .rg(or_8_out));
  or or_8 (or_8_out, cg2, in_1);
  Random #(.width(2), .seed(5)) random_2 (.clk(in_3), .out(random_2_out));  // open: next, clr
  Random #(.width(2), .seed(12315)) random_3 (.clk(counter_5_carry), .out(random_3_out));  // open: next, clr
  Multiplexer #(.width(8), .enable("false")) multiplexer_11 (
    .in0(x), .in1(oldx), .out({ballX, multiplexer_11_out}), .sel(or_9_out));
  or or_9 (or_9_out, switch_x, switch_y);
  check_collision check_collision_1 (
    .x(x), .y(y), .bat_left(out_14), .bat_right(out_15), .out_8(col), .top(top), .center(center), .bot(bot));
  Multiplexer #(.width(8), .enable("false")) multiplexer_12 (
    .in0(y), .in1(oldy), .out({ballY, multiplexer_12_out}), .sel(or_7_out));
  Multiplexer #(.width(3), .disabled(0), .enable("false")) multiplexer_13 (
    .in0(3'b011), .in1(3'b101), .out(multiplexer_13_out), .sel(xor_2_out));
  xor xor_2 (xor_2_out, vx[2], switch_x);
  not not_7 (not_7_out, counter_1_q);
  Counter #(.width(1), .max('h1), .ongoal("stay")) counter_1 (
    .Q(counter_1_q), .clk(and_13_out), .clr(or_10_out));  // open: load, D, count, carry
  and and_13 (and_13_out, center, ~or_10_out);  // AND_Gate
  or or_10 (or_10_out, top, bot);
  Multiplexer #(.width(5), .disabled(0), .enable("false")) multiplexer_14 (
    .in0(out_14), .in1(5'b01110), .out(multiplexer_14_out), .sel(ch));
  assign bit_extender_1_out = {{3{1'b0}}, random_2_out};  // Bit_Extender bit_extender_1
  Comparator #(.width(2), .mode("unsigned")) comparator_9 (
    .a(random_3_out), .b(2'b01), .gt(comparator_9_gt));  // open: eq, lt
  Multiplexer #(.width(3), .enable("false")) multiplexer_15 (
    .in0(multiplexer_13_out), .in1(multiplexer_8_out), .out(new_vx), .sel(not_7_out));
  Counter #(.width(5), .max('h1d), .ongoal("stay")) counter_2 (
    .load(multiplexer_9_out), .D(multiplexer_14_out), .count(multiplexer_10_out), .Q(out_14), .clk(in_3));  // open: carry, clr
  Subtractor #(.width(5)) subtractor_3 (
    .a(main_1_out_8), .b(bit_extender_1_out), .out(subtractor_3_out));  // open: bin, bout
  Adder #(.width(5)) adder_3 (.a(main_1_out_8), .b(bit_extender_1_out), .out(adder_3_out));  // open: cin, cout
  Negator #(.width(3)) negator_1 (.in(vx), .out(negator_1_out));
  Negator #(.width(3)) negator_2 (.in(vy), .out(negator_2_out));
  Multiplexer #(.width(5), .disabled(0), .enable("false")) multiplexer_16 (
    .in0(subtractor_3_out), .in1(adder_3_out), .out(multiplexer_16_out), .sel(comparator_9_gt));
  Multiplexer #(.width(5), .disabled(0), .enable("false")) multiplexer_17 (
    .in0(multiplexer_16_out), .in1(main_1_out_8), .out(multiplexer_17_out), .sel(comparator_9_gt));
  assign bit_extender_2_out = {{5{negator_1_out[2]}}, negator_1_out};  // Bit_Extender bit_extender_2
  assign bit_extender_3_out = {{5{negator_2_out[2]}}, negator_2_out};  // Bit_Extender bit_extender_3
  Multiplexer #(.width(5), .disabled(0), .enable("false")) multiplexer_18 (
    .in0(main_1_out_8), .in1(multiplexer_17_out), .out(multiplexer_18_out), .sel(in_5));
  Comparator #(.width(5), .mode("unsigned")) comparator_10 (
    .a(multiplexer_18_out), .b(out_15), .gt(comparator_10_gt), .eq(comparator_10_eq), .lt(comparator_10_lt));
  Random #(.width(2), .seed(12315)) random_4 (.out(random_4_out));  // open: clk, next, clr
  Comparator #(.width(2), .mode("unsigned")) comparator_11 (.a(random_4_out), .b(2'b01));  // open: gt, eq, lt
  Adder adder_4 (.a(x), .b(bit_extender_2_out), .out(adder_4_out));  // open: cin, cout
  Adder adder_5 (.a(y), .b(bit_extender_3_out), .out(adder_5_out));  // open: cin, cout
  update_vy update_vy_1 (.old_vy(vy), .\output (new_vy), .top(top), .center(center), .bot(bot));
  Multiplexer #(.disabled(0), .enable("false")) multiplexer_19 (
    .in0(and_7_out), .in1(comparator_10_lt), .out(multiplexer_19_out), .sel(in_4));
  Multiplexer #(.disabled(0), .enable("false")) multiplexer_20 (
    .in0(and_12_out), .in1(not_8_out), .out(multiplexer_20_out), .sel(in_4));
  not not_8 (not_8_out, comparator_10_eq);
  Counter #(.width(4), .max('hf), .ongoal("load")) counter_3 (
    .count(in_3), .carry(counter_3_carry), .clk(in_3));  // open: load, D, Q, clr
  Counter #(.width(2), .max('h3), .ongoal("load")) counter_4 (
    .count(in_3), .carry(counter_4_carry), .clk(in_3));  // open: load, D, Q, clr
  check_collision check_collision_2 (
    .x(adder_4_out), .y(y), .bat_left(out_14), .bat_right(out_15), .out_8(check_collision_2_out_8));  // open: top, center, bot
  check_collision check_collision_3 (
    .x(x), .y(adder_5_out), .bat_left(out_14), .bat_right(out_15), .out_8(check_collision_3_out_8));  // open: top, center, bot
  Multiplexer #(.disabled(0), .enable("false")) multiplexer_21 (
    .in0(multiplexer_19_out), .in1(1'b1), .out(multiplexer_21_out), .sel(ch2));
  Multiplexer #(.disabled(0), .enable("false")) multiplexer_22 (
    .in0(multiplexer_20_out), .in1(1'b0), .out(multiplexer_22_out), .sel(ch2));
  and and_14 (and_14_out, ~ch, multiplexer_23_out);  // AND_Gate
  Multiplexer #(.disabled(0), .enable("false")) multiplexer_23 (
    .in0(in_3), .in1(multiplexer_27_out), .out(multiplexer_23_out), .sel(in_4));
  Multiplexer #(.select(2), .disabled(0), .enable("false")) multiplexer_24 (
    .in0(counter_3_carry), .in1(counter_4_carry), .in2(in_3), .in3(in_3), .out(multiplexer_24_out),
    .sel(state));
  Random #(.width(5)) random_5 (.clk(in_3), .out(random_5_out));  // open: next, clr
  Counter #(.width(6), .max('h3f), .ongoal("load")) counter_5 (
    .D(random_6_out), .count(in_3), .carry(counter_5_carry), .clk(in_3));  // open: load, Q, clr
  Random #(.width(6)) random_6 (.clk(in_3), .out(random_6_out));  // open: next, clr
  and and_15 (and_15_out, ~check_collision_2_out_8, col);  // AND_Gate
  or or_11 (switch_x, and_15_out, and_16_out);
  and and_16 (and_16_out, check_collision_2_out_8, col, check_collision_3_out_8);
  or or_12 (switch_y, and_16_out, and_17_out);
  and and_17 (and_17_out, ~check_collision_3_out_8, col);  // AND_Gate
  Multiplexer #(.width(5), .disabled(0), .enable("false")) multiplexer_25 (
    .in0(out_15), .in1(5'b01110), .out(multiplexer_25_out), .sel(ch2));
  Counter #(.width(5), .max('h1d), .ongoal("stay")) counter_6 (
    .load(multiplexer_21_out), .D(multiplexer_25_out), .count(multiplexer_22_out), .Q(out_15),
    .clk(multiplexer_26_out));  // open: carry, clr
  Multiplexer #(.disabled(0), .enable("false")) multiplexer_26 (
    .in0(and_14_out), .in1(ch2), .out(multiplexer_26_out), .sel(ch2));
  Multiplexer #(.disabled(0), .enable("false")) multiplexer_27 (
    .in0(multiplexer_24_out), .in1(multiplexer_28_out), .out(multiplexer_27_out), .sel(in_5));
  Multiplexer #(.select(2), .disabled(0), .enable("false")) multiplexer_28 (
    .in0(counter_7_carry), .in1(counter_8_carry), .in2(counter_9_carry), .in3(counter_9_carry),
    .out(multiplexer_28_out), .sel(state));
  Counter #(.width(5), .max('h1f), .ongoal("load")) counter_7 (
    .D(random_5_out), .count(in_3), .carry(counter_7_carry), .clk(in_3));  // open: load, Q, clr
  Counter #(.width(4), .max('hf), .ongoal("load")) counter_8 (
    .D(random_7_out), .count(in_3), .carry(counter_8_carry), .clk(in_3));  // open: load, Q, clr
  Random #(.width(4)) random_7 (.clk(in_3), .out(random_7_out));  // open: next, clr
  Random #(.width(2)) random_8 (.clk(in_3), .out(random_8_out));  // open: next, clr
  Multiplexer #(.disabled(0), .enable("false")) multiplexer_29 (
    .in0(clock), .in1(in_3), .out(multiplexer_29_out), .sel(d_ff_1_q));
  Counter #(.width(2), .max('h3), .ongoal("load")) counter_9 (
    .D(random_8_out), .count(in_3), .carry(counter_9_carry), .clk(in_3));  // open: load, Q, clr
  D_Flip_Flop d_ff_1 (.clk(multiplexer_29_out), .D(ch), .Q(d_ff_1_q));  // open: Qn, preset, en, reset
  or or_13 (or_13_out, _1, _2);
  Register #(.width(1)) register_1 (.D(ch), .Q(ch2), .clk(in_3));  // open: en, clr
  Counter #(.width(7), .max('h7f), .ongoal("stay")) counter_10 (
    .carry(counter_10_carry), .clk(in_3), .clr(d_ff_1_q));  // open: load, D, count, Q
  assign controlled_buffer_1_out = counter_10_carry ? in_3 : 1'bz;  // Controlled_Buffer controlled_buffer_1
  Counter #(.width(2), .max('h2)) counter_11 (
    .carry(counter_11_carry), .clk(controlled_buffer_1_out));  // open: load, D, count, Q, clr
  Counter #(.width(4), .max('hf), .ongoal("stay"), .trigger("falling")) counter_12 (
    .Q(out_12), .clk(col), .clr(or_13_out));  // open: load, D, count, carry
  Counter #(.width(4), .max('h9), .trigger("falling")) counter_13 (
    .Q(out_7[7:4]), .clk(counter_14_carry), .clr(in_1));  // open: load, D, count, carry
  Counter #(.width(4), .max('h9)) counter_14 (
    .Q(out_7[3:0]), .carry(counter_14_carry), .clk(_1), .clr(in_1));  // open: load, D, count
  and and_18 (_1, not_9_out, not_10_out, p1g);
  not not_9 (not_9_out, col);
  not not_10 (not_10_out, p2g);
  not not_11 (not_11_out, d_ff_2_q);
  D_Flip_Flop d_ff_2 (.clk(controlled_buffer_1_out), .D(not_11_out), .Q(d_ff_2_q));  // open: Qn, preset, en, reset
  Comparator #(.width(4), .mode("unsigned")) comparator_12 (.a(out_12), .b(4'b0101), .gt(state[0]));  // open: eq, lt
  Comparator #(.width(4), .mode("unsigned")) comparator_13 (.a(out_12), .b(4'b1010), .gt(state[1]));  // open: eq, lt
  D_Flip_Flop d_ff_3 (.clk(not_11_out), .D(not_12_out), .Q(d_ff_3_q));  // open: Qn, preset, en, reset
  not not_12 (not_12_out, d_ff_3_q);
  Multiplexer #(.disabled(0), .enable("false")) multiplexer_30 (
    .in0(not_12_out), .in1(counter_11_carry), .out(multiplexer_30_out), .sel(state[0]));
  Multiplexer #(.disabled(0), .enable("false")) multiplexer_31 (
    .in0(multiplexer_30_out), .in1(not_11_out), .out(multiplexer_31_out), .sel(state[1]));
  Multiplexer #(.select(2), .disabled(0), .enable("false")) multiplexer_32 (
    .in0(multiplexer_31_out), .in1(1'b0), .in2(1'b0), .in3(1'b0), .out(clock), .sel(out_13));
  Counter #(.width(4), .max('h9), .trigger("falling")) counter_15 (
    .Q(out_8[7:4]), .clk(counter_16_carry), .clr(in_1));  // open: load, D, count, carry
  Counter #(.width(4), .max('h9)) counter_16 (
    .Q(out_8[3:0]), .carry(counter_16_carry), .clk(_2), .clr(in_1));  // open: load, D, count
  and and_19 (_2, not_14_out, not_13_out, p2g);
  not not_13 (not_13_out, col);
  not not_14 (not_14_out, p1g);
  Counter #(.width(1), .max('h1), .ongoal("stay")) counter_17 (
    .Q(counter_17_q), .carry(counter_17_q), .clk(in_1));  // open: load, D, count, clr
  Multiplexer #(.width(2), .disabled(0), .enable("false")) multiplexer_33 (
    .in0(2'b01), .in1(2'b00), .out(multiplexer_33_out), .sel(counter_17_q));
  Multiplexer #(.width(2), .disabled(0), .enable("false")) multiplexer_34 (
    .in0(multiplexer_33_out), .in1(2'b10), .out(multiplexer_34_out), .sel(out_7[4]));
  Multiplexer #(.width(2), .disabled(0), .enable("false")) multiplexer_35 (
    .in0(multiplexer_34_out), .in1(2'b11), .out(out_13), .sel(out_8[4]));

  assign out_10 = {5{1'b0}};

  // Other names for the same wires on the sheet: p1win = out_7[4]; p2win = out_8[4]; AI = in_4; bat1[4:0] = out_14;
  //   bat2[4:0] = out_15; cg = in_2; Keyboard[6:0] = keyboard_in; reset = in_1; stateg[1:0] = out_13;
  //   Stupidness = in_5; z = in_3

  // Notes on the sheet:
  //   Keyboard
  //   Ball motion
  //   vx calc
  //   Bat collision
  //   vy calc
  //   Bat's logic
  //   AI faults
  //   Speed of game
  //   Score calculating
endmodule

module reflect (
  input  [2:0] speed,
  input  cout,
  output [2:0] out_3,
  output out_4,
  output p2goal,
  output p1goal
);

  wire and_2_out, not_1_out;
  wire [2:0] negator_1_out;

  Negator #(.width(3)) negator_1 (.in(speed), .out(negator_1_out));
  xor xor_1 (out_4, speed[2], cout);
  Multiplexer #(.width(3), .enable("false")) multiplexer_1 (.in0(speed), .in1(negator_1_out), .out(out_3), .sel(out_4));
  and and_1 (p2goal, out_4, speed[2]);
  and and_2 (and_2_out, out_4, cout);
  not not_1 (not_1_out, p2goal);
  and and_3 (p1goal, not_1_out, and_2_out);
endmodule

module motion (
  input  [7:0] coord,
  input  [2:0] speed,
  output [7:0] new_cords,
  output [2:0] new_speed,
  output p1goal,
  output p2goal
);

  wire adder_1_cout, reflect_1_out_4;
  wire [7:0] adder_1_out, bit_extender_1_out;

  assign bit_extender_1_out = {{5{speed[2]}}, speed};  // Bit_Extender bit_extender_1
  Adder adder_1 (.a(coord), .b(bit_extender_1_out), .out(adder_1_out), .cout(adder_1_cout));  // open: cin
  reflect reflect_1 (
    .speed(speed), .cout(adder_1_cout), .out_3(new_speed), .out_4(reflect_1_out_4), .p2goal(p2goal),
    .p1goal(p1goal));
  Multiplexer #(.width(8), .enable("false")) multiplexer_1 (
    .in0(adder_1_out), .in1(coord), .out(new_cords), .sel(reflect_1_out_4));
endmodule

module check_collision (
  input  [7:0] x,
  input  [7:0] y,
  input  [4:0] bat_left,
  input  [4:0] bat_right,
  output top,
  output center,
  output bot,
  output out_8
);

  wire and_1_out, and_2_out, and_3_out, and_4_out, and_5_out, and_6_out, and_7_out, and_8_out, bl, br, cl,
       cr, lc, or_1_out, or_2_out, rc, tl, tr;
  wire [4:0] inc_1_out_2, inc_2_out_2, inc_3_out_2, inc_4_out_2;

  inc inc_1 (.in_1(bat_right), .out_2(inc_1_out_2));
  inc inc_2 (.in_1(bat_left), .out_2(inc_2_out_2));
  inc inc_3 (.in_1(inc_2_out_2), .out_2(inc_3_out_2));
  inc inc_4 (.in_1(inc_1_out_2), .out_2(inc_4_out_2));
  Comparator #(.width(5)) comparator_1 (.a(y[7:3]), .b(bat_left), .eq(bl));  // open: gt, lt
  Comparator #(.width(5)) comparator_2 (.a(y[7:3]), .b(inc_2_out_2), .eq(cl));  // open: gt, lt
  Comparator #(.width(5)) comparator_3 (.a(y[7:3]), .b(inc_3_out_2), .eq(tl));  // open: gt, lt
  Comparator #(.width(5), .mode("unsigned")) comparator_4 (.a(x[7:3]), .b(5'b11100), .eq(rc));  // open: gt, lt
  Comparator #(.width(5)) comparator_5 (.a(y[7:3]), .b(bat_right), .eq(br));  // open: gt, lt
  Comparator #(.width(5)) comparator_6 (.a(y[7:3]), .b(inc_1_out_2), .eq(cr));  // open: gt, lt
  Comparator #(.width(5)) comparator_7 (.a(y[7:3]), .b(inc_4_out_2), .eq(tr));  // open: gt, lt
  Comparator #(.width(5), .mode("unsigned")) comparator_8 (.a(x[7:3]), .b(5'b00011), .eq(lc));  // open: gt, lt
  or or_1 (or_1_out, bl, cl, tl);
  or or_2 (or_2_out, br, cr, tr);
  and and_1 (and_1_out, lc, or_1_out);
  and and_2 (and_2_out, rc, or_2_out);
  and and_3 (and_3_out, lc, tl);
  or or_3 (out_8, and_1_out, and_2_out);
  or or_4 (top, and_3_out, and_4_out);
  and and_4 (and_4_out, rc, tr);
  or or_5 (center, and_6_out, and_5_out);
  and and_5 (and_5_out, rc, cr);
  and and_6 (and_6_out, lc, cl);
  or or_6 (bot, and_7_out, and_8_out);
  and and_7 (and_7_out, lc, bl);
  and and_8 (and_8_out, rc, br);
endmodule

module update_vy (
  input  top,
  input  center,
  input  bot,
  input  [2:0] old_vy,
  output [2:0] \output 
);

  wire nor_1_out;

  assign \output  = top ? 3'b001 : 3'bz;  // Controlled_Buffer controlled_buffer_1
  assign \output  = center ? 3'b000 : 3'bz;  // Controlled_Buffer controlled_buffer_2
  assign \output  = bot ? 3'b111 : 3'bz;  // Controlled_Buffer controlled_buffer_3
  nor nor_1 (nor_1_out, bot, center, top);
  assign \output  = nor_1_out ? old_vy : 3'bz;  // Controlled_Buffer controlled_buffer_4
endmodule
