// Logisim project ai + keyboard.circ as structural Verilog: 6 circuits, main circuit main
module main (
  input  [7:0] x,
  input  [7:0] y,
  input  state,
  output [4:0] out_4
);

  wire and_3_out, and_4_out, and_5_out, and_6_out, cdm_8_mark5_1_p1, cdm_8_mark5_1_p2, cdm_8_mark5_1_p4,
       cdm_8_mark5_1_p5, cdm_8_mark5_1_p6, cdm_8_mark5_1_p7, cdm_8_mark5_1_p8, cdm_8_mark5_1_p9,
       cdm_8_mark5_1_p10, clear, clock, data, decoder_1_out1, decoder_1_out2, decoder_1_out3, decoder_1_out4,
       I_O_sel, ins, nand_1_out, not_1_out, RAM, rd_wr, register_3_q;
  wire [2:0] register_4_q;
  wire [3:0] I_O_adr;
  wire [7:0] bit_extender_1_out, cdm_8_mark5_1_p13, cdm_8_mark5_1_p14, I_O_data, register_1_q, register_2_q;
  wire [7:4] cdm_8_mark5_1_p12;

  Decoder #(.select(4), .disabled(0), .enable("false")) decoder_1 (
    .out1(decoder_1_out1), .out2(decoder_1_out2), .out3(decoder_1_out3), .out4(decoder_1_out4), .sel(I_O_adr));  // open: out0, out5, out6, out7, out8, out9, out10, out11, out12, out13, out14, out15
  // Probe on cdm_8_mark5_1_p1
  and and_1 (I_O_sel, ~nand_1_out, clock, data);  // AND_Gate
  // Probe on cdm_8_mark5_1_p2
  // Probe on cdm_8_mark5_1_p4
  // Probe on cdm_8_mark5_1_p6
  Clock clock_1 (.out(clock));
  and and_2 (RAM, nand_1_out, data);
  Register register_1 (.D(y), .Q(register_1_q), .clk(state));  // open: en, clr
  // Probe on cdm_8_mark5_1_p5
  // Probe on cdm_8_mark5_1_p7
  // Probe on cdm_8_mark5_1_p8
  // CdM_8_mark5 cdm_8_mark5_1: pin names not known; wires that end beside it: cdm_8_mark5_1_p1, cdm_8_mark5_1_p2, clock, cdm_8_mark5_1_p4, cdm_8_mark5_1_p5, cdm_8_mark5_1_p6, cdm_8_mark5_1_p7, cdm_8_mark5_1_p8, cdm_8_mark5_1_p9, cdm_8_mark5_1_p10, rd_wr, {cdm_8_mark5_1_p12, I_O_adr}, cdm_8_mark5_1_p13, cdm_8_mark5_1_p14
  assign cdm_8_mark5_1_p14 = rd_wr ? I_O_data : 8'bz;  // Controlled_Buffer controlled_buffer_1
  nand nand_1 (nand_1_out, cdm_8_mark5_1_p12[4], cdm_8_mark5_1_p12[5], cdm_8_mark5_1_p12[6], cdm_8_mark5_1_p12[7]);
  and and_3 (and_3_out, rd_wr, I_O_sel, decoder_1_out1);
  and and_4 (and_4_out, rd_wr, decoder_1_out2, I_O_sel);
  and and_5 (and_5_out, rd_wr, decoder_1_out3, I_O_sel);
  and and_6 (and_6_out, ~rd_wr, I_O_sel, decoder_1_out4);  // AND_Gate
  Register register_2 (.D(x), .Q(register_2_q), .clk(state));  // open: en, clr
  Register #(.width(1), .trigger("falling")) register_3 (
    .D(1'b1), .en(and_6_out), .Q(register_3_q), .clk(state));  // open: clr
  Decoder #(.disabled(0)) decoder_2 (.out0(ins), .out1(data), .sel(cdm_8_mark5_1_p9), .en(cdm_8_mark5_1_p10));
  assign I_O_data = not_1_out ? cdm_8_mark5_1_p13 : 8'bz;  // Controlled_Buffer controlled_buffer_2
  not not_1 (not_1_out, rd_wr);
  assign bit_extender_1_out = {{7{1'b0}}, register_3_q};  // Bit_Extender bit_extender_1
  assign I_O_data = and_3_out ? bit_extender_1_out : 8'bz;  // Controlled_Buffer controlled_buffer_3
  assign I_O_data = and_4_out ? register_2_q : 8'bz;  // Controlled_Buffer controlled_buffer_4
  assign I_O_data = and_5_out ? register_1_q : 8'bz;  // Controlled_Buffer controlled_buffer_5
  Register #(.trigger("falling")) register_4 (
    .D(I_O_data), .Q({out_4, register_4_q}), .clk(and_6_out));  // open: en, clr
  ROM rom_1 (.addr({cdm_8_mark5_1_p12, I_O_adr}), .data(I_O_data), .sel(ins));
  RAM #(.bus("separate")) ram_1 (
    .addr({cdm_8_mark5_1_p12, I_O_adr}), .din(I_O_data), .data(I_O_data), .sel(RAM), .clk(clock), .ld(rd_wr),
    .clr(clear));  // open: str
  // Probe on I_O_data

  // Notes on the sheet:
  //   contents of rom_1 (hex, n*v repeats v):
  //   d0 f1 b0 0 e1 d d1 7f d0 f4 a1 ee 0 d0 f2 b0 d1 f0 34 98 d1 7f 44 d1 f3 b5 d2 1 7 0 e0 27 19 e2 2c 7
  //   88 ee 1d d0 f4 a1 ee 0 d 86 19
endmodule

module keyboard (
  input  [6:0] in_1,
  output [1:0] out_2
);

  wire comparator_1_eq, comparator_2_eq, comparator_3_eq, comparator_4_eq;

  Comparator #(.width(7)) comparator_1 (.a(in_1), .b(7'b1110011), .eq(comparator_1_eq));  // open: gt, lt
  Comparator #(.width(7)) comparator_2 (.a(in_1), .b(7'b1001011), .eq(comparator_2_eq));  // open: gt, lt
  Comparator #(.width(7)) comparator_3 (.a(in_1), .b(7'b1110111), .eq(comparator_3_eq));  // open: gt, lt
  Comparator #(.width(7)) comparator_4 (.a(in_1), .b(7'b1000110), .eq(comparator_4_eq));  // open: gt, lt
  Transistor #(.\type ("n")) transistor_1 (.in(1'b1), .out(out_2[0]), .gate(comparator_1_eq));
  Pull_Resistor pull_resistor_1 (.node(out_2[0]));
  Transistor #(.\type ("n"), .gate("br")) transistor_2 (.in(1'b1), .out(out_2[0]), .gate(comparator_2_eq));
  Transistor #(.\type ("n")) transistor_3 (.in(1'b1), .out(out_2[1]), .gate(comparator_3_eq));
  Pull_Resistor pull_resistor_2 (.node(out_2[1]));
  Transistor #(.\type ("n"), .gate("br")) transistor_4 (.in(1'b1), .out(out_2[1]), .gate(comparator_4_eq));
  // Probe on out_2
endmodule

module keyboardR (
  input  [6:0] in_1,
  output [1:0] out_2
);

  wire comparator_1_eq, comparator_2_eq, comparator_3_eq, comparator_4_eq;

  Comparator #(.width(7)) comparator_1 (.a(in_1), .b(7'b1101100), .eq(comparator_1_eq));  // open: gt, lt
  Comparator #(.width(7)) comparator_2 (.a(in_1), .b(7'b0110100), .eq(comparator_2_eq));  // open: gt, lt
  Comparator #(.width(7)) comparator_3 (.a(in_1), .b(7'b1101111), .eq(comparator_3_eq));  // open: gt, lt
  Comparator #(.width(7)) comparator_4 (.a(in_1), .b(7'b1001001), .eq(comparator_4_eq));  // open: gt, lt
  Transistor #(.\type ("n")) transistor_1 (.in(1'b1), .out(out_2[0]), .gate(comparator_1_eq));
  Pull_Resistor pull_resistor_1 (.node(out_2[0]));
  Transistor #(.\type ("n"), .gate("br")) transistor_2 (.in(1'b1), .out(out_2[0]), .gate(comparator_2_eq));
  Transistor #(.\type ("n")) transistor_3 (.in(1'b1), .out(out_2[1]), .gate(comparator_3_eq));
  Pull_Resistor pull_resistor_2 (.node(out_2[1]));
  Transistor #(.\type ("n"), .gate("br")) transistor_4 (.in(1'b1), .out(out_2[1]), .gate(comparator_4_eq));
  // Probe on out_2
endmodule

module test (
);

  wire clock_1_out;
  wire [6:0] keyboard_1_data;

  Clock clock_1 (.out(clock_1_out));
  Keyboard keyboard_1 (.clk(clock_1_out), .data(keyboard_1_data));  // open: re, clr, avail
  // Probe on keyboard_1_data
endmodule

module keyboardBML (
  input  [6:0] in_1,
  output [1:0] out_2
);

  wire comparator_1_eq, comparator_2_eq, comparator_3_eq, comparator_4_eq;

  Comparator #(.width(7)) comparator_1 (.a(in_1), .b(7'b1100101), .eq(comparator_1_eq));  // open: gt, lt
  Comparator #(.width(7)) comparator_2 (.a(in_1), .b(7'b1000011), .eq(comparator_2_eq));  // open: gt, lt
  Comparator #(.width(7)) comparator_3 (.a(in_1), .b(7'b0110010), .eq(comparator_3_eq));  // open: gt, lt
  Comparator #(.width(7)) comparator_4 (.a(in_1), .b(7'b1100100), .eq(comparator_4_eq));  // open: gt, lt
  Transistor #(.\type ("n")) transistor_1 (.in(1'b1), .out(out_2[0]), .gate(comparator_1_eq));
  Pull_Resistor pull_resistor_1 (.node(out_2[0]));
  Transistor #(.\type ("n"), .gate("br")) transistor_2 (.in(1'b1), .out(out_2[0]), .gate(comparator_2_eq));
  Transistor #(.\type ("n")) transistor_3 (.in(1'b1), .out(out_2[1]), .gate(comparator_3_eq));
  Pull_Resistor pull_resistor_2 (.node(out_2[1]));
  Transistor #(.\type ("n"), .gate("br")) transistor_4 (.in(1'b1), .out(out_2[1]), .gate(comparator_4_eq));
  // Probe on out_2
endmodule

module keyboardBMR (
  input  [6:0] in_1,
  output [1:0] out_2
);

  wire comparator_1_eq, comparator_2_eq, comparator_3_eq, comparator_4_eq;

  Comparator #(.width(7)) comparator_1 (.a(in_1), .b(7'b1110000), .eq(comparator_1_eq));  // open: gt, lt
  Comparator #(.width(7)) comparator_2 (.a(in_1), .b(7'b0110111), .eq(comparator_2_eq));  // open: gt, lt
  Comparator #(.width(7)) comparator_3 (.a(in_1), .b(7'b0110110), .eq(comparator_3_eq));  // open: gt, lt
  Comparator #(.width(7)) comparator_4 (.a(in_1), .b(7'b0111011), .eq(comparator_4_eq));  // open: gt, lt
  Transistor #(.\type ("n")) transistor_1 (.in(1'b1), .out(out_2[0]), .gate(comparator_1_eq));
  Pull_Resistor pull_resistor_1 (.node(out_2[0]));
  Transistor #(.\type ("n"), .gate("br")) transistor_2 (.in(1'b1), .out(out_2[0]), .gate(comparator_2_eq));
  Transistor #(.\type ("n")) transistor_3 (.in(1'b1), .out(out_2[1]), .gate(comparator_3_eq));
  Pull_Resistor pull_resistor_2 (.node(out_2[1]));
  Transistor #(.\type ("n"), .gate("br")) transistor_4 (.in(1'b1), .out(out_2[1]), .gate(comparator_4_eq));
  // Probe on out_2
endmodule
