// Logisim project ai.circ as structural Verilog: 2 circuits, main circuit main
module main (
  input  in_1
);

  wire cdm_8_mark5_1_p1, cdm_8_mark5_1_p2, cdm_8_mark5_1_p4, cdm_8_mark5_1_p5, cdm_8_mark5_1_p6,
       cdm_8_mark5_1_p7, cdm_8_mark5_1_p8, cdm_8_mark5_1_p9, cdm_8_mark5_1_p13, clock, not_1_out;
  wire [7:0] cdm_8_mark5_1_p10, cdm_8_mark5_1_p11, cdm_8_mark5_1_p12, controlled_buffer_2_out, undriven;

  // Probe on cdm_8_mark5_1_p1
  Clock clock_1 (.out(clock));
  // Probe on cdm_8_mark5_1_p2
  // Probe on cdm_8_mark5_1_p4
  // Probe on cdm_8_mark5_1_p6
  // Probe on cdm_8_mark5_1_p5
  // Probe on cdm_8_mark5_1_p8
  // Probe on cdm_8_mark5_1_p7
  // CdM_8_mark5 cdm_8_mark5_1: pin names not known; wires that end beside it: cdm_8_mark5_1_p1, cdm_8_mark5_1_p2, clock, cdm_8_mark5_1_p4, cdm_8_mark5_1_p5, cdm_8_mark5_1_p6, cdm_8_mark5_1_p7, cdm_8_mark5_1_p8, cdm_8_mark5_1_p9, cdm_8_mark5_1_p10, cdm_8_mark5_1_p11, cdm_8_mark5_1_p12, cdm_8_mark5_1_p13, cdm_8_mark5_1_p10
  not not_1 (not_1_out, cdm_8_mark5_1_p9);
  assign cdm_8_mark5_1_p12 = cdm_8_mark5_1_p9 ? undriven : 8'bz;  // Controlled_Buffer controlled_buffer_1
  // Probe on cdm_8_mark5_1_p10
  assign controlled_buffer_2_out = not_1_out ? cdm_8_mark5_1_p11 : 8'bz;  // Controlled_Buffer controlled_buffer_2
  RAM ram_1 (.addr(cdm_8_mark5_1_p10), .data(controlled_buffer_2_out), .sel(cdm_8_mark5_1_p13));  // open: clk, ld, clr
  RAM #(.bus("separate")) ram_2 (
    .din(undriven), .data(controlled_buffer_2_out), .clk(clock), .ld(cdm_8_mark5_1_p9), .clr(in_1));  // open: addr, str, sel
endmodule

module keyboard (
  input  bus_0
);

  wire clock, controlled_buffer_1_out, keyboard_1_avail;
  wire [6:0] keyboard_1_data;

  Clock clock_1 (.out(clock));
  Keyboard keyboard_1 (
    .clk(controlled_buffer_1_out), .avail(keyboard_1_avail), .data(keyboard_1_data));  // open: re, clr
  assign controlled_buffer_1_out = keyboard_1_avail ? clock : 1'bz;  // Controlled_Buffer controlled_buffer_1
  TTY tty_1 (.data(keyboard_1_data), .clk(clock), .clr(bus_0));  // open: we
endmodule
